# Fritzing sketch 3D-PAWS_Muon-v20251105 (saved by Fritzing 0.9.10b)

parts:
  Part27 = Adafruit RFM9x LoRa Radio [part_number="Adafruit #3072 and #3073"]
  S1 = Toggle Switch [package=THT]
  Part28 = Adafruit SDIO microSD Breakout
  J1 = Raspberry Pi Header 40pin [form="♂ (male)" package=THT]
  LED1 = LED - 5mm [color="Red (633nm)" current=0.030 package="5 mm [THT]"]
  R7 = Resistor [tolerance=±5% resistance=330 package="1206 [SMD]"]
  U12 = Honeywell SS451A [chip_label="Hall Effect Sensor" package=THT]
  U14 = Honeywell SS451A [chip_label="Hall Effect Sensor" package=THT]
  R9 = Resistor [tolerance=±5% resistance=1k power=0.25 package=THT]
  R10 = Resistor [tolerance=±5% resistance=1k power=0.25 package=THT]
  C8 = Ceramic Capacitor [capacitance=0.1mF voltage=35V package="100 mil [THT, multilayer]"]
  C9 = Ceramic Capacitor [capacitance=0.1mF package="100 mil [THT, multilayer]"]

nets:
  VIN: Part27.VIN, J1.5V
  GND: Part27.GND, S1.COM, Part28.GND, J1.GND, LED1.cathode
  N1: Part27.DIO0, J1.GIPO21
  N2: Part27.SCK, J1.GIPO17
  N3: Part27.MISO, J1.GIPO15
  N4: Part27.MOSI, J1.GIPO14
  N5: Part27.CS, J1.GIPO16
  N6: Part27.RST, J1.GIPO20
  N7: S1.L1, J1.GIPO7
  3V3: Part28.3.3V, J1.3v3, J1.3V3
  N8: Part28.SCLK, J1.GIPO11
  N9: Part28.DO, J1.GIPO9
  N10: Part28.DI, J1.GIPO10
  N11: Part28.CS, J1.GIPO8
  N12: J1.GIPO5, J1.GIPO6
  N13: J1.GIPO25, R7.Pin_0
  N14: U12.pin1, C9.1
  N15: U12.pin2, C9.0
  N16: U12.pin3, R10.Pin_1
  N17: U14.pin2, C8.0
  N18: U14.pin3, R9.Pin_1

notes:
  Console Enable
  Pin Name Pin Name
  26 D17/A2 -> 39 Ground
  SD
  Pin Name SD Board
  17 3v3 3v
  19 SPI MOSI SI
  21 SPI MISO SO
  23 SPI SCK CLK
  25 GND GND
  24 D29/A6 CS
  Grove D26
  37 IOEX_PB7 Do Not Use
  13 A5/D14 Open
  Grove D5
  29 A0/D19 Option 1, Rain2, Distance, Raw
  31 A1/D18 Option 2, Raw
  GPS - Do Not Use
  Pin Name
  16 D24 Serial TX
  18 D25 Serial RX
  Grove D18
  12 D6 Open
  35 D26 Open
  Rain Gauge 1 (D4)
  SS451A Omnipolar Digital Hall-effect Sensor
  Anemometer (D5)
  SS451A Omnipolar Digital Hall-effect Sensor
  Grove Shield Digital Connectors
  GRV Pin 1 Pin2
  PWM 32-D5 (Wind) 33-D4 (Rain)
  D5 29-A0/D19 (Option 1) 31-A1/D18 (Option 2)
  D16 36-D3 (LoRa CS) 11-D2 (LoRa SPI1 CLK)
  D18 12-D6 Open 35-D26 (Open)
  UART 8-D9/TX (LoRa SPI1 MOSI) 10-D10/RX (LoRa SPI1 MISO)
  D26 37-IOEX_PB7 Do Not Use 13-A5/D14 Open
  D22 15 D27 16 D24
  D24 18 D25 26 D17
  Grove PWN
  32 D5 Wind
  33 D4 Rain
  7 IOEX_PA0
  Grove D22
  15 D27 Relay Trigger
  16 D24 GPS TX - Do Not Use
  Grove D24
  18 D25 GPS RX - Do Not Use
  22 D17 LED
  Grove I2C
  3 SDA
  5 SCL
  1 3.3v
  9 GND
  Muon to LoRa Interconnet Pinout
  Pin Muon Name LoRa Pin
  8 MOSI SPI1 D9 MOSI (Master Out Slave In)
  10 MISO SPI1 D10 MISO (Master Im Slave Out)
  11 SCK SPI1 D2 SCK
  36 CS SPI1 D3 SS (Slave Select)
  38 D21 RST (Reset)
  40 D20 DIO/IRQ
  30 GND GND
  2 5V Vin
  Muon
  On board I2C addresses
  0x28: STUSB4500 USB-C power controller
  0x36: MAX17043 Fuel Gauge
  0x48: TMP112A temperature sensor
  0x61: KG200Z LoRaWAN radio
  0x69: AM1805 RTC/Watchdog
  0x6B: bq24195 Power Management IC (PMIC)

custom parts:
  Adafruit RFM9x LoRa Radio: Sending data over long distances is like magic, and now you can be a magician with this range of powerful and easy-to-use radio modules. Sure, sometimes you want to talk to a computer (a good time to use WiFi) or perhaps communicate with a Phone (choose Bluetooth Low Energy!) but what if you want to send data very far? Most WiFi, Bluetooth, Zigbee and other wireless chipsets use 2.4GHz, which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
  Raspberry Pi Header 40pin: Raspberry Pi 40 pin header - for creating your own shields.
  Honeywell SS451A: Omnipolar Digital Hall-effect Sensor
