# Fritzing sketch Particle_FullStation-20260830 (saved by Fritzing 0.9.10b)

parts:
  R1 = Resistor [tolerance=±5% resistance=1k power=0.25 package=THT]
  C1 = Ceramic Capacitor [capacitance=0.1mF package="100 mil [THT, multilayer]"]
  Part4 = SI1145 Digital UV Index + IR + Visible Light Sensor [part_number=1777]  # not connected
  R2 = Resistor [tolerance=±5% resistance=1k power=0.25 package=THT]
  C2 = Ceramic Capacitor [capacitance=0.1mF package="100 mil [THT, multilayer]"]
  U4 = Honeywell SS451A [chip_label="Hall Effect Sensor" package=THT]
  U7 = Honeywell SS451A [chip_label="Hall Effect Sensor" package=THT]
  Part12 = OLED Monochrome 128x32 I2C [part_number=931]  # not connected
  Boron2 = Particle Boron
  Part14 = Adafruit Adalogger FeatherWing [part_number="Adafruit #2922"]
  Part17 = Adafruit SHT31-D [part_number="Adafruit #2857"]
  X2 = USB Connectors [package=usb-a-s-nosilk-female]  # not connected
  BAT2 = Battery Holders [package=lipo-1100mAh]  # not connected
  JP3 = Header 2 [package=jst-2-pth-ns]  # not connected
  JP4 = Header 2 [package=jst-2-pth-ns]  # not connected
  Part19 = USB Mini-B Breakout [part_number=1764]  # not connected
  Part20 = Adafruit BMP280 [part_number="Adafruit #2651"]
  Part21 = Adafruit BMP388 [part_number="Adafruit #3966"]
  Part22 = Adafruit BME280 [part_number="Adafruit #2652"]
  Part23 = Adafruit MCP9808 [part_number="Adafruit #5027"]
  Part24 = Adafruit HTU21D-F Temperature & Humidity Sensor [part_number="Adafruit #1899"]
  Part25 = Adafruit PMSA003I Air Quality Breakout [part_number="Adafruit #4632"]  # not connected
  OLED_I2C3 = OLED 128x64 I2C Monochrome Display  # not connected
  Part26 = Adafruit RFM9x LoRa Radio [part_number="Adafruit #3072 and #3073"]
  Adafruit_HDC3021_Precision_Temperature_Humidity_Sensor1 = Adafruit HDC3021 Precision Temperature Humidity Sensor [part_number=#5989]
  S2 = Toggle Switch [package=THT]  # not connected
  PCA1 = Adafruit PCA9548 8-Channel STEMMA QT / Qwiic I2C Multiplexer [part_number=5626]  # not connected
  C3 = Ceramic Capacitor [capacitance=0.1mF voltage=35V package="100 mil [THT, multilayer]"]
  R3 = Resistor [tolerance=±5% power=0.25 resistance=1k package=THT]
  U8 = Honeywell SS451A [chip_label="Hall Effect Sensor" package=THT]
  Adafruit_DS2482S-800_8_Channel_I2C_to_1-Wire_Bus_Adapter1 = Adafruit DS2482S-800 8 Channel I2C to 1-Wire Bus Adapter [part_number=#6027]  # not connected
  Part40 = Adafruit USB Type C Breakout [part_number=4090]
  Adafruit_BMP581_Temperature_and_Pressure_Sensor5 = Adafruit BMP581 Temperature and Pressure Sensor [part_number=#6407]
  Part43 = Adafruit SHT4x [part_number="Adafruit #4885"]
  Part44 = Adafruit LTR390 UV Light Sensor [part_number="Adafruit #4831"]

nets:
  N1: R1.Pin_0, C1.1
  N2: R1.Pin_1, U7.pin3
  N3: C1.0, C2.0, U4.pin2, U7.pin2
  N4: R2.Pin_0, C2.1, U4.pin1, U7.pin1, C3.1, R3.Pin_0, U8.pin1
  N5: R2.Pin_1, U4.pin3
  N6: Boron2.SCK, Part14.SCK
  N7: Boron2.MO, Part14.MOSI
  N8: Boron2.MI, Part14.MISO
  N9: Boron2.SDA, Part14.SDA
  N10: Boron2.SCL, Part14.SCL
  N11: Boron2.D5, Part14.CS
  N12: Boron2.D6, Part26.DIO0
  GND: Part17.GND, Part20.GND, Part21.GND, Part22.GND, Part23.GND, Part24.GND
  VCC: Part17.VCC, Part20.VCC, Part21.VCC, Part22.VCC, Part23.VCC, Part24.VCC
  N13: Part17.SDA, Part20.SDI/SDA, Part20.CS, Part21.SDI/SDA, Part22.SDI/SDA, Part23.SDA, Part24.SDA
  N14: Part17.SCL, Part20.SCK/SCL, Part21.SCK/SCL, Part22.SCK/SCL, Part23.SCL, Part24.SCL
  GND_2: Adafruit_HDC3021_Precision_Temperature_Humidity_Sensor1.GND, Part44.GND
  VCC_2: Adafruit_HDC3021_Precision_Temperature_Humidity_Sensor1.VCC, Part44.VCC
  N15: Adafruit_HDC3021_Precision_Temperature_Humidity_Sensor1.SDA, Part44.SDA
  N16: Adafruit_HDC3021_Precision_Temperature_Humidity_Sensor1.SCL, Part44.SCL
  N17: C3.0, U8.pin2
  N18: R3.Pin_1, U8.pin3
  N19: Part40.SBU2, Part40.SBU1
  GND_3: Adafruit_BMP581_Temperature_and_Pressure_Sensor5.GND, Part43.GND
  VCC_3: Adafruit_BMP581_Temperature_and_Pressure_Sensor5.VCC, Part43.VCC
  N20: Adafruit_BMP581_Temperature_and_Pressure_Sensor5.SDI/SDA, Part43.SDA
  N21: Adafruit_BMP581_Temperature_and_Pressure_Sensor5.SCK/SCL, Part43.SCL

notes:
  MCP9808 High Accuracy Temperature Sensor
  I2C 7-bit address 0x18
  HTU21D-F Temperature & Humidity Sensor
  I2C 7-bit address 0x40
  Anemometer (A2)
  SS451A Omnipolar Digital Hall-effect Sensor
  Wind Vane (as5600-so_ek_ab)
  Rotory Position Sensor
  I2C address 0x36
  Adafruit SI1145
  Light Sensor
  I2C 7-bit address 0x60
  Rain Gauge 1 (A3)
  SS451A Omnipolar Digital Hall-effect Sensor
  Only one OLED at a time
  Feather Adalogger Shield
  Pin - D5 SD CS
  Pin - SPI MOSI
  Pin - SPI MISO
  Pin - SPI CLK
  Pin - SDA
  Pin - SCL
  Console Enable
  Set D8 to Ground
  D5 Used by SD Card Chip Select
  BMP280
  Barometic Pressure
  Altitude Sensor
  Temperature
  I2C 7-bit address
  Default = 0x77
  SD0 to GND = 0x76
  G 3 S S
  N V D C
  D 3 A L
  G 3 D D
  N V 3 2
  D 3
  G 3 A A
  N V 1 0
  D 3
  G 3 D D
  N V 5 4
  D 3
  S S 3 G
  C D V N
  L A 3 D
  R T 3 G
  X X V N
  X X 3 D
  A A 3 G
  2 3 V N
  3 D
  A A 3 G
  4 5 V N
  3 D
  SHT31 Temperature & Humidy
  I2C address 0x44
  I2C address 0x45 ADR Pin High
  TF02Pro (5v)
  Distance Sensor
  I2C address 0x10
  Large Lipo Battery
  Voltage Regulator
  Solar Panel
  5V TR TR HB
  WatchDog Monitor
  BMP388
  Barometic Pressure
  Altitude Sensor
  Temperature
  I2C 7-bit address
  Default = 0x77
  SD0 to GND = 0x76
  Adafruit's Grove Shield FeatherWing for Particle Mesh
  BME288
  Barometic Pressure
  Altitude Sensor
  Temperature
  Humidity
  I2C 7-bit address
  Default = 0x76
  SD0 to GND = 0x77
  Adafruit OLED64
  Display SSD1306
  I2C 7-bit address 0x3D
  Adafruit OLED 128x32
  Display SSD1306
  I2C 7-bit address 0x3C
  Particle Full Station Schematic
  Version 2026-08-30
  OptionPin 1 - pin A4
  0 = No sensor
  1 = raw (op1r - average 5 samples spaced 10ms)
  2 = 2nd rain gauge (rg2)
  5 = 5M distance sensor (ds, dsr)
  10 = 10m distance sensor (ds, dsr)
  LoRa Feather Pinouts
  MISO to D4 MISO
  MOSI to D3 MOSI
  SCK to D2 SCK
  CS to D10 ChipSel
  RST to D9 Reset
  G0 to D6 DIO/IRQ
  D8 = Serial Console (Ground Pin to Enable)
  D7 = On Board LED - Unused - Not on Grove Shield
  D6 = LoRa IRQ - Not on Grove Shield
  D5 = SD Card Chip Select
  D4 = SPI1 MISO - LoRa
  D3 = SPI1 MOSI - LoRa
  D2 = SPI1 SCK - LoRa
  D1 = I2C SCL
  D0 = I2C SDA
  A0 = WatchDog Monitor/Relay Reset Trigger
  A1 = WatchDog Monitor Heartbeat
  A2 = Interrupt For Anemometer (Wind Speed)
  A3 = Interrupt For Rain Gauge
  A4 = Option 1 Pin
  A5 = Option 2 Pin
  D13 = SPIO CLK SD Card
  D12 = SPI0 MOSI SD Card
  D11 = SPI0 MISO SD Card
  D10 = UART1 RX - LoRa CS
  D9 = UART1 TX - LoRa Reset
  AdaFruit PMSA003I
  Air Quality Sensor
  I2C address 0x12
  HDC302x
  Temperature
  Humidy
  I2C address 0x46 A1=1 A0=0
  I2C address 0x47 A1=1 A0=1
  DFRobot B_LUX_V30B
  0-200klx LUX Sensor
  I2C 7-bit address 0x4A
  Option 2 A5
  0 = No sensor (Pin in use if pm25aqi air quality dectected)
  1 = raw (op2r - average 5 samples spaced 10ms)
  2 = read Voltaic battery voltage (vbv)
  D7 On board LED
  Tinovi PM-WCS-3-I2C
  Soil Moisture & Temperature
  I2C address 0x63
  Up to 8 supported
  1 per MUX channel
  Tinovi Leaf-Wet-I2C
  I2C address 0x61
  Tinovi SOIL-MULTI-5-I2C
  Soil Moisture & Temperature
  I2C address 0x65
  Power Option 3.3v or 5v
  I2C MUX
  Adafruit PCA9548
  or
  Grove TCA9548A
  I2C address 0x70
  Opt1 - Rain Gauge 2 (A4)
  SS451A Omnipolar Digital Hall-effect Sensor
  AQS Mode
  I2C to 1-Wire MUX
  Adafruit DS2482S-800
  I2C address 0x1F
  Supports 8 1-Wire Dallas
  Temperature Sensors
  DS18B20, 1 per Channel.
  Use SBU on post-2023 Voltaic. Otherwise D+
  USBC Breakout
  Connect to Voltaic Battery
  BMP581 Temperature & Pressure Sensor
  I2C 7-bit address 0x47-0x46
  SHT45 Temperature & Humidity Sensor
  I2C 7-bit address 0x44
  DFRobot SENS0562
  BH1750 LUX Sensor
  I2C 7-bit address 0x23
  Adafruit LTR390
  UV Light Sensor
  I2C 7-bit address 0x53

custom parts:
  SI1145 Digital UV Index + IR + Visible Light Sensor: The SI1145 is a new sensor from SiLabs with a calibrated light sensing algorithm that can calculate UV Index. It doesn't contain an actual UV sensing element, instead it approximates it based on visible & IR light from the sun. We took this outside a couple days and compared the calculated UV index with the news-reported index and found it was very accurate! It's a digital sensor that works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
  Honeywell SS451A: Omnipolar Digital Hall-effect Sensor
  OLED Monochrome 128x32 I2C: These displays are small, only about 1" diagonal, but very readable due to the high contrast of an OLED display. This display is made of 128x32 individual white OLED pixels, each one is turned on or off by the controller chip. Because the display makes its own light, no backlight is required. This reduces the power required to run the OLED and is why the display has such high contrast; we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
  Particle Boron: The Boron LTE is a powerful LTE CAT-M1 enabled development kit that can act as either a standalone cellular device or LTE enabled gateway, repeater, or endpoint for a Particle Mesh networks. Equipped with the Nordic nRF52840 and u-blox SARA 410 processors, the Boron has built-in battery charging circuitry which makes it easier to connect a Li-Po battery and 20 mixed signal GPIOs to interface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
  Adafruit Adalogger FeatherWing: This is the Adalogger FeatherWing: it adds both a battery-backed Real Time Clock and micro SD card storage to any Feather main board. This FeatherWing will make it real easy to add datalogging to any of our existing Feathers. You get both an I2C real time clock (PCF8523) with 32KHz crystal and battery backup, and a microSD socket that connects to the SPI port pins (+ extra pin for CS). Tested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
  Adafruit SHT31-D: Sensirion Temperature/Humidity sensors are some of the finest & highest-accuracy devices you can get. And, finally we have some that have a true I2C interface for easy reading. The SHT31-D sensor has an excellent ±2% relative humidity and ±0.3°C accuracy for most uses. We now use the version with a PTFE filter, it'll stay clean while still allowing humidity measurements to work Unlike earlier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
  USB Mini-B Breakout: Simple but effective - this breakout board has a USB Mini-B connector, with all 5 pins broken out. Great for pairing with a microcontroller with USB support, or adding USB 5V power to a project.
  Adafruit BMP280: Bosch has stepped up their game with their new BMP280 sensor, an environmental sensor with temperature, barometric pressure that is the next generation upgrade to the BMP085/BMP180/BMP183. This sensor is great for all sorts of weather sensing and can even be used in both I2C and SPI! This precision sensor from Bosch is the best low-cost, precision sensing solution for measuring barometric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
  Adafruit BMP388: Bosch has been a leader in barometric pressure sensors, from the BMP085. BMP180, and BMP280... now we've got the next generation, the Adafruit BMP388 Precision Barometric Pressure sensor. As you would expect, this sensor is similar to its earlier versions but even better. The BMP388 has better precision than ever, which makes it excellent for environmental sensing or as a precision altimeter.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
  Adafruit BME280: Bosch has stepped up their game with their new BME280 sensor, an environmental sensor with temperature, barometric pressure and humidity! This sensor is great for all sorts of indoor environmental sensing and can even be used in both I2C and SPI! This precision sensor from Bosch is the best low-cost sensing solution for measuring humidity with ±3% accuracy, barometric pressure with ±1 hPa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
  Adafruit MCP9808: The MCP9808 digital temperature sensor is one of the more accurate/precise we've ever seen, with a typical accuracy of ±0.25°C over the sensor's -40°C to +125°C range and precision of +0.0625°C. They work great with any microcontroller using standard I2C. With three address jumpers on the back, you can connect up to 8 to a single I2C bus without address collisions. Best of all, a wide voltage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
  Adafruit HTU21D-F Temperature & Humidity Sensor: It's summer and you're sweating and your hair's all frizzy and all you really want to know is why the weatherman said this morning that today's relative humidity would max out at a perfectly reasonable 52% when it feels more like 77%. Enter the HTU21D-F Temperature + Humidity Sensor - the best way to prove the weatherman wrong! This I2C digital humidity sensor is an accurate and intelligent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
  Adafruit PMSA003I Air Quality Breakout: Breathe easy, knowing that you can track and sense the quality of the air around you with this Adafruit PMSA003I Air Quality Breakout. This sensor is great for monitoring air quality, in a compact plug-in format. Best of all, unlike almost all other sensors we've seen that are UART interface, this one is I2C interface, which makes it a great match for single board Linux computers like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
  Adafruit RFM9x LoRa Radio: Sending data over long distances is like magic, and now you can be a magician with this range of powerful and easy-to-use radio modules. Sure, sometimes you want to talk to a computer (a good time to use WiFi) or perhaps communicate with a Phone (choose Bluetooth Low Energy!) but what if you want to send data very far? Most WiFi, Bluetooth, Zigbee and other wireless chipsets use 2.4GHz, which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
  Adafruit HDC3021 Precision Temperature Humidity Sensor: We stock a large number of Temperature/Humidity sensors, so you're probably wondering why another one? Well, this Adafruit HDC3021 Precision Temperature & Humidity Sensor breakout features the highest accuracy & precision one we've see so far! It has the TI HDC302x series chip with typical 0.5% accuracy for the RH sensor (with 0.19% long-term drift) and ±0.1°C typical accuracy for the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
  Adafruit PCA9548 8-Channel STEMMA QT / Qwiic I2C Multiplexer: You just found the perfect I2C sensor, available in a handy chainable Qwiic, or STEMMA QT package, and you want to wire up two or three or more of them to your microcontroller when you realize "Uh oh, this chip has a fixed I2C address, and from what I know about I2C, you cannot have two devices with the same address on the same SDA/SCL pins!" Are you out of luck? You would be, if you didn't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
  Adafruit DS2482S-800 8 Channel I2C to 1-Wire Bus Adapter: This is a DS2482S-800 Stemma QT board that uses a I2C-to-1W controller chip, with 8 selectable channels, built-in parasitic-power-pullups, adjustable I2C address and a wide operating voltage range! You can easily connect it to an existing I2C bus and then use the breakout pads to attach multiple DS18B20's, or pair it with our 1-Wire chaining breakouts for fancier experimentation. You're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
  Adafruit USB Type C Breakout: Adafruit breakout board for USB Type C socket.
  Adafruit BMP581 Temperature and Pressure Sensor: Bosch has been a leader in barometric pressure sensors, from the BMP085. BMP180, BMP280, BMP388, BMP390... now we've got the next generation, the Adafruit BMP58x Precision Barometric Pressure and Altimeter Breakout. As you would expect, this sensor is similar to its earlier versions but even better. The BMP581 has better precision than ever, which makes it excellent for environmental sensing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
  Adafruit SHT4x: Sensirion Temperature/Humidity sensors are some of the finest & highest-accuracy devices you can get. And finally, we have some that have a true I2C interface for easy reading. The SHT40 and SHT45 sensors are the fourth generation (started at the SHT10 and worked its way up to the top!). The SHT40 has an excellent ±1.8% typical relative humidity accuracy from 25 to 75% and ±0.2 °C typical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
  Adafruit LTR390 UV Light Sensor: The LTR390 is one of the few low-cost UV sensors available, and it's a pretty nice one! With both ambient light and UVA sensing with a peak spectral response between 300 and 350nm. You can use it for measuring how much sun you can get before needing to covering up. Unlike the Si1145, this sensor will not give you UV Index readings. However, the Si1145 does UV Index approximations based on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
